# Fritzing sketch schema_arduino (saved by Fritzing 0.9.3b)
breadboards: 1

parts:
  Composant1 = Arduino Uno (Rev3)
  R1 = Resistor [tolerance=±5% resistance=220 package=THT]
  R2 = Resistor [tolerance=±5% resistance=220 package=THT]
  R3 = Resistor [tolerance=±5% resistance=220 package=THT]
  LED1 = LED - 5mm [color="Red (633nm)" package="5 mm [THT]"]
  LED3 = LED - 5mm [color="Red (633nm)" package="5 mm [THT]"]
  LED4 = LED - 5mm [color="Red (633nm)" package="5 mm [THT]"]

nets:
  N1: Composant1.GND, LED1.cathode, LED3.cathode, LED4.cathode
  N2: Composant1.D2, R3.Pin_1
  N3: Composant1.D3_PWM, R1.Pin_1
  N4: Composant1.D4, R2.Pin_1
  N5: R1.Pin_0, LED3.anode
  N6: R2.Pin_0, LED4.anode
  N7: R3.Pin_0, LED1.anode
